# Fritzing sketch watertank-level (saved by Fritzing 1.0.6)
circuit board: 8.46667cm x 5.64444cm

parts:
  M1 = AJ-SR04M Module [part_number=AJ-SR04M]
  M2 = AJ-SR04M Module [part_number=AJ-SR04M]
  A1 = Esp32-c3 super mini

nets:
  N1: M1.GND, A1.Pin_15
  N2: M1.Echo, A1.Pin_12
  N3: M1.Trig, A1.Pin_13
  VCC: M1.VCC, M2.VCC, A1.Pin_16
  N4: M2.Echo, A1.Pin_5
  N5: M2.Trig, A1.Pin_4

custom parts:
  AJ-SR04M Module: AJ-SR04M Ultrasonic Distance Measuring Sensor Controller Module, 3-5V DC.
  Esp32-c3 super mini: ESP32-C3 Development Board ESP32 SuperMini Development Board ESP32 Development Board WiFi Bluetooth.
